// Logisim project DD1_Proj_2.circ as structural Verilog
module main (
  input  [7:0] in_1,
  input  [7:0] in_2,
  input  in_3,
  input  in_4,
  input  [1:0] in_5
);

  wire adder_1_cout, button_1_out, button_2_out, button_3_out, Clkout, Done, EA, EB, EP, LA, LB,
       multiplexer_3_out, multiplexer_8_out, Psel, rst, shift_register_1_out, shift_register_1_q0,
       shift_register_1_q1, shift_register_1_q2, shift_register_1_q3, shift_register_1_q4,
       shift_register_1_q5, shift_register_1_q6, xor_1_out, Z_flag;
  wire [1:0] Sel;
  wire [3:0] Five, Four, multiplexer_5_out, multiplexer_6_out, multiplexer_7_out, One, Three, Two;
  wire [7:0] l_8bit_2_s_complementor_9531c271_1_output, l_8bit_2_s_complementor_9531c271_2_output,
       multiplexer_1_out, multiplexer_4_out;
  wire [15:0] adder_1_out, controlled_buffer_1_out, left_shift_register_aa06cfc5_1_out, multiplexer_2_out,
       register_1_q;

  // Probe on left_shift_register_aa06cfc5_1_out
  L_8bit_2_s_Complementor_9531c271 l_8bit_2_s_complementor_9531c271_1 (
    .Input(in_1), .Output(l_8bit_2_s_complementor_9531c271_1_output));  // open: out_3
  Multiplexer #(.width(8)) multiplexer_1 (
    .in0(in_1), .in1(l_8bit_2_s_complementor_9531c271_1_output), .out(multiplexer_1_out), .sel(in_1[7]));
  // Probe on multiplexer_1_out
  Left_Shift_Register_aa06cfc5 left_shift_register_aa06cfc5_1 (
    .D9(1'b0), .D8(1'b0), .D7(multiplexer_1_out[7]), .D6(multiplexer_1_out[6]), .D5(multiplexer_1_out[5]),
    .D4(multiplexer_1_out[4]), .D3(multiplexer_1_out[3]), .D2(multiplexer_1_out[2]),
    .D1(multiplexer_1_out[1]), .D0(multiplexer_1_out[0]), .Input(1'b0), .D15(1'b0), .D14(1'b0), .D13(1'b0),
    .EN(EA), .Load(LA), .Clk(Clkout), .D12(1'b0), .D11(1'b0), .D10(1'b0),
    .Out(left_shift_register_aa06cfc5_1_out));
  Adder #(.width(16)) adder_1 (
    .a(left_shift_register_aa06cfc5_1_out), .b(register_1_q), .out(adder_1_out), .cin(multiplexer_3_out),
    .cout(adder_1_cout));
  Multiplexer #(.width(16)) multiplexer_2 (.in0({16{1'b0}}), .in1(adder_1_out), .out(multiplexer_2_out), .sel(Psel));
  Multiplexer multiplexer_3 (.in0(adder_1_cout), .in1(1'b0), .out(multiplexer_3_out), .sel(rst));
  // Probe on adder_1_out
  Register #(.width(16)) register_1 (.D(multiplexer_2_out), .en(EP), .Q(register_1_q), .clk(Clkout), .clr(rst));
  Shift_Register shift_register_1 (
    .shift(EB), .in(1'b0), .clk(Clkout), .out(shift_register_1_out), .load(LB), .d0(multiplexer_4_out[7]),
    .q0(shift_register_1_q0), .d1(multiplexer_4_out[6]), .q1(shift_register_1_q1), .d2(multiplexer_4_out[5]),
    .q2(shift_register_1_q2), .d3(multiplexer_4_out[4]), .q3(shift_register_1_q3), .d4(multiplexer_4_out[3]),
    .q4(shift_register_1_q4), .d5(multiplexer_4_out[2]), .q5(shift_register_1_q5), .d6(multiplexer_4_out[1]),
    .q6(shift_register_1_q6), .d7(multiplexer_4_out[0]));  // open: clr, q7
  // Probe on register_1_q
  L_8bit_2_s_Complementor_9531c271 l_8bit_2_s_complementor_9531c271_2 (
    .Input(in_2), .Output(l_8bit_2_s_complementor_9531c271_2_output));  // open: out_3
  Multiplexer #(.width(8)) multiplexer_4 (
    .in0(in_2), .in1(l_8bit_2_s_complementor_9531c271_2_output), .out(multiplexer_4_out), .sel(in_2[7]));
  // Probe on multiplexer_4_out
  Clock clock_1 (.out(Clkout));
  nor nor_1 (Z_flag, shift_register_1_q0, shift_register_1_q1, shift_register_1_q2, shift_register_1_q3, shift_register_1_q4, shift_register_1_q5, shift_register_1_q6, shift_register_1_out);
  xor xor_1 (xor_1_out, in_1[7], in_2[7]);
  Button button_1 (.out(button_1_out));
  Button button_2 (.out(button_2_out));
  Button button_3 (.out(button_3_out));
  assign controlled_buffer_1_out = Done ? register_1_q : 16'bz;  // Controlled_Buffer controlled_buffer_1
  Control_unit control_unit_1 (
    .reset(in_3), .BTNC(button_1_out), .b0(shift_register_1_out), .Clk(Clkout), .BTNL(button_2_out),
    .BTNR(button_3_out), .Enable(in_4), .Z_flag(Z_flag), .rst(rst), .LA(LA), .LB(LB), .Psel(Psel), .Sel(Sel),
    .EB(EB), .EP(EP), .EA(EA), .Done(Done));
  BCD bcd_1 (
    .Bin_0(controlled_buffer_1_out[0]), .Bin_1(controlled_buffer_1_out[1]),
    .Bin_2(controlled_buffer_1_out[2]), .Bin_3(controlled_buffer_1_out[3]),
    .Bin_4(controlled_buffer_1_out[4]), .Bin_5(controlled_buffer_1_out[5]),
    .Bin_6(controlled_buffer_1_out[6]), .Bin_7(controlled_buffer_1_out[7]),
    .Bin_8(controlled_buffer_1_out[8]), .Bin_9(controlled_buffer_1_out[9]),
    .Bin_10(controlled_buffer_1_out[10]), .Bin_11(controlled_buffer_1_out[11]),
    .Bin_12(controlled_buffer_1_out[12]), .Bin_13(controlled_buffer_1_out[13]),
    .Bin_14(controlled_buffer_1_out[14]), .Bin_15(controlled_buffer_1_out[15]), .BCD_ones(One),
    .BCD_Tens(Two), .BCD_Hundereds(Three), .BCD_Thousands(Four), .BCD_Ten_Thousands(Five));
  // Probe on in_5
  Multiplexer #(.select(2), .width(4)) multiplexer_5 (
    .in0(Three), .in1(Four), .in2(Five), .in3(Five), .out(multiplexer_5_out), .sel(in_5));
  Multiplexer #(.select(2), .width(4)) multiplexer_6 (
    .in0(Two), .in1(Three), .in2(Four), .in3(Four), .out(multiplexer_6_out), .sel(in_5));
  Multiplexer #(.select(2), .width(4)) multiplexer_7 (
    .in0(One), .in1(Two), .in2(Three), .in3(Three), .out(multiplexer_7_out), .sel(in_5));
  Multiplexer multiplexer_8 (.in0(1'b1), .in1(1'b0), .out(multiplexer_8_out), .sel(xor_1_out));
  // Probe on multiplexer_8_out
  Hex_Digit_Display hex_digit_display_1 (.value(multiplexer_6_out));  // open: dp
  Hex_Digit_Display hex_digit_display_2 (.value(multiplexer_7_out), .dp(multiplexer_7_out[0]));
  _7_Segment_Display u_7_segment_display_1 (.g(multiplexer_8_out));  // open: f, a, b, e, d, c, dp
  Hex_Digit_Display hex_digit_display_3 (.value(multiplexer_5_out), .dp(multiplexer_5_out[0]));
  // Pins of 1 and 4 bits meet at multiplexer_5_out
  // Pins of 1 and 4 bits meet at multiplexer_7_out

  // Other names for the same wires on the sheet: SW15 = in_1[7]; SW7 = in_2[7]
endmodule

// LSR
module Left_Shift_Register_aa06cfc5 (
  input  Load,
  input  Clk,
  input  EN,
  input  D14,
  input  D12,
  input  D10,
  input  D8,
  input  D6,
  input  D4,
  input  D2,
  input  D0,
  input  Input,
  input  D15,
  input  D13,
  input  D11,
  input  D9,
  input  D7,
  input  D5,
  input  D3,
  input  D1,
  output [15:0] Out
);

  wire ClkT, multiplexer_1_out, multiplexer_2_out, multiplexer_3_out, multiplexer_4_out, multiplexer_5_out,
       multiplexer_6_out, multiplexer_7_out, multiplexer_8_out, multiplexer_9_out, multiplexer_10_out,
       multiplexer_11_out, multiplexer_12_out, multiplexer_13_out, multiplexer_14_out, multiplexer_15_out,
       multiplexer_16_out, undriven;

  and and_1 (ClkT, Clk, Clk);
  Multiplexer multiplexer_1 (.in0(Out[14]), .in1(D15), .out(multiplexer_1_out), .sel(Load));
  D_Flip_Flop #(.trigger("high")) d_ff_1 (.clk(ClkT), .D(multiplexer_1_out), .Q(Out[15]));  // open: Qn, preset, reset
  Multiplexer multiplexer_2 (.in0(Out[13]), .in1(D14), .out(multiplexer_2_out), .sel(Load));
  D_Flip_Flop #(.trigger("high")) d_ff_2 (.clk(ClkT), .D(multiplexer_2_out), .Q(Out[14]));  // open: Qn, preset, reset
  Multiplexer multiplexer_3 (.in0(Out[12]), .in1(D13), .out(multiplexer_3_out), .sel(Load));
  D_Flip_Flop #(.trigger("high")) d_ff_3 (.clk(ClkT), .D(multiplexer_3_out), .Q(Out[13]));  // open: Qn, preset, reset
  Multiplexer multiplexer_4 (.in0(Out[11]), .in1(D12), .out(multiplexer_4_out), .sel(Load));
  D_Flip_Flop #(.trigger("high")) d_ff_4 (
    .clk(ClkT), .D(multiplexer_4_out), .Q(Out[12]), .reset(undriven));  // open: Qn, preset
  Multiplexer multiplexer_5 (.in0(Out[10]), .in1(D11), .out(multiplexer_5_out), .sel(Load));
  D_Flip_Flop #(.trigger("high")) d_ff_5 (.clk(ClkT), .D(multiplexer_5_out), .Q(Out[11]));  // open: Qn, preset, reset
  Multiplexer multiplexer_6 (.in0(Out[9]), .in1(D10), .out(multiplexer_6_out), .sel(Load));
  D_Flip_Flop #(.trigger("high")) d_ff_6 (.clk(ClkT), .D(multiplexer_6_out), .Q(Out[10]));  // open: Qn, preset, reset
  Multiplexer multiplexer_7 (.in0(Out[8]), .in1(D9), .out(multiplexer_7_out), .sel(Load));
  D_Flip_Flop #(.trigger("high")) d_ff_7 (.clk(ClkT), .D(multiplexer_7_out), .Q(Out[9]));  // open: Qn, preset, reset
  Multiplexer multiplexer_8 (.in0(Out[7]), .in1(D8), .out(multiplexer_8_out), .sel(Load));
  D_Flip_Flop #(.trigger("high")) d_ff_8 (.clk(ClkT), .D(multiplexer_8_out), .Q(Out[8]));  // open: Qn, preset, reset
  Multiplexer multiplexer_9 (.in0(Out[6]), .in1(D7), .out(multiplexer_9_out), .sel(Load));
  D_Flip_Flop #(.trigger("high")) d_ff_9 (.clk(ClkT), .D(multiplexer_9_out), .Q(Out[7]));  // open: Qn, preset, reset
  Multiplexer multiplexer_10 (.in0(Out[5]), .in1(D6), .out(multiplexer_10_out), .sel(Load));
  D_Flip_Flop #(.trigger("high")) d_ff_10 (.clk(ClkT), .D(multiplexer_10_out), .Q(Out[6]));  // open: Qn, preset, reset
  Multiplexer multiplexer_11 (.in0(Out[4]), .in1(D5), .out(multiplexer_11_out), .sel(Load));
  D_Flip_Flop #(.trigger("high")) d_ff_11 (.clk(ClkT), .D(multiplexer_11_out), .Q(Out[5]));  // open: Qn, preset, reset
  Multiplexer multiplexer_12 (.in0(Out[3]), .in1(D4), .out(multiplexer_12_out), .sel(Load));
  D_Flip_Flop #(.trigger("high")) d_ff_12 (.clk(ClkT), .D(multiplexer_12_out), .Q(Out[4]));  // open: Qn, preset, reset
  Multiplexer multiplexer_13 (.in0(Out[2]), .in1(D3), .out(multiplexer_13_out), .sel(Load));
  D_Flip_Flop #(.trigger("high")) d_ff_13 (.clk(ClkT), .D(multiplexer_13_out), .Q(Out[3]));  // open: Qn, preset, reset
  Multiplexer multiplexer_14 (.in0(Out[1]), .in1(D2), .out(multiplexer_14_out), .sel(Load));
  D_Flip_Flop #(.trigger("high")) d_ff_14 (.clk(ClkT), .D(multiplexer_14_out), .Q(Out[2]));  // open: Qn, preset, reset
  Multiplexer multiplexer_15 (.in0(Out[0]), .in1(D1), .out(multiplexer_15_out), .sel(Load));
  D_Flip_Flop #(.trigger("high")) d_ff_15 (.clk(ClkT), .D(multiplexer_15_out), .Q(Out[1]));  // open: Qn, preset, reset
  Multiplexer multiplexer_16 (.in0(Input), .in1(D0), .out(multiplexer_16_out), .sel(Load));
  D_Flip_Flop #(.trigger("high")) d_ff_16 (.clk(ClkT), .D(multiplexer_16_out), .Q(Out[0]));  // open: Qn, preset, reset

  assign EN = Clk;

  // Other names for the same wires on the sheet: LoadT = Load
endmodule

module L_8bit_2_s_Complementor_9531c271 (
  input  [7:0] Input,
  output [7:0] Output,
  output out_3
);

  wire [7:0] not_1_out;

  assign not_1_out = ~Input;  // NOT_Gate not_1, 8 bits wide
  Adder adder_1 (.a(not_1_out), .b({8{1'b0}}), .out(Output), .cin(1'b1), .cout(out_3));
endmodule

module L_16bit_2_s_Complementor_591851de (
  input  [15:0] Input,
  output [15:0] Output
);

  wire [15:0] not_1_out;

  assign not_1_out = ~Input;  // NOT_Gate not_1, 16 bits wide
  Adder #(.width(16)) adder_1 (.a(not_1_out), .b({16{1'b0}}), .out(Output), .cin(1'b1));  // open: cout
endmodule

module LSR_8_bit_8d4ba8a3 (
  input  Load,
  input  Clk,
  input  D6,
  input  D4,
  input  D2,
  input  D0,
  input  Input,
  input  D7,
  input  D5,
  input  D3,
  input  D1,
  input  EN,
  output [7:0] Out
);

  wire multiplexer_1_out, multiplexer_2_out, multiplexer_3_out, multiplexer_4_out, multiplexer_5_out,
       multiplexer_6_out, multiplexer_7_out, multiplexer_8_out;

  Multiplexer multiplexer_1 (.in0(Out[6]), .in1(D7), .out(multiplexer_1_out), .sel(Load));
  D_Flip_Flop d_ff_1 (.clk(Clk), .D(multiplexer_1_out), .Q(Out[7]));  // open: Qn, preset, reset
  Multiplexer multiplexer_2 (.in0(Out[5]), .in1(D6), .out(multiplexer_2_out), .sel(Load));
  D_Flip_Flop d_ff_2 (.clk(Clk), .D(multiplexer_2_out), .Q(Out[6]));  // open: Qn, preset, reset
  Multiplexer multiplexer_3 (.in0(Out[4]), .in1(D5), .out(multiplexer_3_out), .sel(Load));
  D_Flip_Flop d_ff_3 (.clk(Clk), .D(multiplexer_3_out), .Q(Out[5]));  // open: Qn, preset, reset
  Multiplexer multiplexer_4 (.in0(Out[3]), .in1(D4), .out(multiplexer_4_out), .sel(Load));
  D_Flip_Flop d_ff_4 (.clk(Clk), .D(multiplexer_4_out), .Q(Out[4]));  // open: Qn, preset, reset
  Multiplexer multiplexer_5 (.in0(Out[2]), .in1(D3), .out(multiplexer_5_out), .sel(Load));
  D_Flip_Flop d_ff_5 (.clk(Clk), .D(multiplexer_5_out), .Q(Out[3]));  // open: Qn, preset, reset
  Multiplexer multiplexer_6 (.in0(Out[1]), .in1(D2), .out(multiplexer_6_out), .sel(Load));
  D_Flip_Flop d_ff_6 (.clk(Clk), .D(multiplexer_6_out), .Q(Out[2]));  // open: Qn, preset, reset
  Multiplexer multiplexer_7 (.in0(Out[0]), .in1(D1), .out(multiplexer_7_out), .sel(Load));
  D_Flip_Flop d_ff_7 (.clk(Clk), .D(multiplexer_7_out), .Q(Out[1]));  // open: Qn, preset, reset
  Multiplexer multiplexer_8 (.in0(Input), .in1(D0), .out(multiplexer_8_out), .sel(Load));
  D_Flip_Flop d_ff_8 (.clk(Clk), .D(multiplexer_8_out), .Q(Out[0]));  // open: Qn, preset, reset

  // Other names for the same wires on the sheet: ClkT = Clk; LoadT = Load
endmodule

module Shift_add32 (
  input  Input_0,
  input  Input_1,
  input  Input_2,
  input  Input_3,
  output out_0,
  output out_1,
  output out_2,
  output out_3
);

  wire comparator_1_gt;
  wire [3:0] adder_1_out;

  Adder #(.width(4)) adder_1 (
    .a(4'b0011), .b({Input_3, Input_2, Input_1, Input_0}), .out(adder_1_out), .cin(1'b0));  // open: cout
  Comparator #(.mode("unsigned"), .width(4)) comparator_1 (
    .a({Input_3, Input_2, Input_1, Input_0}), .b(4'b0100), .gt(comparator_1_gt));  // open: eq, lt
  Multiplexer #(.width(4)) multiplexer_1 (
    .in0({Input_3, Input_2, Input_1, Input_0}), .in1(adder_1_out), .out({out_3, out_2, out_1, out_0}),
    .sel(comparator_1_gt));
endmodule

module BCD (
  input  Bin_0,
  input  Bin_1,
  input  Bin_2,
  input  Bin_3,
  input  Bin_4,
  input  Bin_5,
  input  Bin_6,
  input  Bin_7,
  input  Bin_8,
  input  Bin_9,
  input  Bin_10,
  input  Bin_11,
  input  Bin_12,
  input  Bin_13,
  input  Bin_14,
  input  Bin_15,
  output [3:0] BCD_ones,
  output [3:0] BCD_Tens,
  output [3:0] BCD_Hundereds,
  output [3:0] BCD_Thousands,
  output [3:0] BCD_Ten_Thousands
);

  wire shift_add32_1_out_0, shift_add32_1_out_1, shift_add32_1_out_2, shift_add32_1_out_3,
       shift_add32_2_out_0, shift_add32_2_out_1, shift_add32_2_out_2, shift_add32_2_out_3,
       shift_add32_3_out_0, shift_add32_3_out_1, shift_add32_3_out_2, shift_add32_3_out_3,
       shift_add32_4_out_0, shift_add32_4_out_1, shift_add32_4_out_2, shift_add32_4_out_3,
       shift_add32_5_out_0, shift_add32_5_out_1, shift_add32_5_out_2, shift_add32_5_out_3,
       shift_add32_6_out_0, shift_add32_6_out_1, shift_add32_6_out_2, shift_add32_6_out_3,
       shift_add32_7_out_0, shift_add32_7_out_1, shift_add32_7_out_2, shift_add32_7_out_3,
       shift_add32_8_out_0, shift_add32_8_out_1, shift_add32_8_out_2, shift_add32_8_out_3,
       shift_add32_9_out_0, shift_add32_9_out_1, shift_add32_9_out_2, shift_add32_9_out_3,
       shift_add32_10_out_0, shift_add32_10_out_1, shift_add32_10_out_2, shift_add32_10_out_3,
       shift_add32_11_out_0, shift_add32_11_out_1, shift_add32_11_out_2, shift_add32_11_out_3,
       shift_add32_12_out_0, shift_add32_12_out_1, shift_add32_12_out_2, shift_add32_12_out_3,
       shift_add32_13_out_0, shift_add32_13_out_1, shift_add32_13_out_2, shift_add32_13_out_3,
       shift_add32_14_out_0, shift_add32_14_out_1, shift_add32_14_out_2, shift_add32_14_out_3,
       shift_add32_15_out_0, shift_add32_15_out_1, shift_add32_15_out_2, shift_add32_15_out_3,
       shift_add32_16_out_0, shift_add32_16_out_1, shift_add32_16_out_2, shift_add32_16_out_3,
       shift_add32_17_out_0, shift_add32_17_out_1, shift_add32_17_out_2, shift_add32_17_out_3,
       shift_add32_18_out_0, shift_add32_18_out_1, shift_add32_18_out_2, shift_add32_18_out_3,
       shift_add32_19_out_0, shift_add32_19_out_1, shift_add32_19_out_2, shift_add32_19_out_3,
       shift_add32_20_out_0, shift_add32_20_out_1, shift_add32_20_out_2, shift_add32_20_out_3,
       shift_add32_21_out_0, shift_add32_21_out_1, shift_add32_21_out_2, shift_add32_21_out_3,
       shift_add32_22_out_0, shift_add32_22_out_1, shift_add32_22_out_2, shift_add32_22_out_3,
       shift_add32_23_out_0, shift_add32_23_out_1, shift_add32_23_out_2, shift_add32_23_out_3,
       shift_add32_24_out_0, shift_add32_24_out_1, shift_add32_24_out_2, shift_add32_24_out_3,
       shift_add32_25_out_0, shift_add32_25_out_1, shift_add32_25_out_2, shift_add32_25_out_3,
       shift_add32_26_out_0, shift_add32_26_out_1, shift_add32_26_out_2, shift_add32_26_out_3,
       shift_add32_27_out_0, shift_add32_27_out_1, shift_add32_27_out_2, shift_add32_27_out_3,
       shift_add32_28_out_0, shift_add32_28_out_1, shift_add32_28_out_2, shift_add32_28_out_3,
       shift_add32_29_out_0, shift_add32_29_out_1, shift_add32_29_out_2, shift_add32_29_out_3,
       shift_add32_30_out_0, shift_add32_30_out_1, shift_add32_30_out_2, shift_add32_30_out_3;

  Shift_add32 shift_add32_1 (
    .Input_0(Bin_13), .Input_1(Bin_14), .Input_2(Bin_15), .Input_3(1'b0), .out_0(shift_add32_1_out_0),
    .out_1(shift_add32_1_out_1), .out_2(shift_add32_1_out_2), .out_3(shift_add32_1_out_3));
  Shift_add32 shift_add32_2 (
    .Input_0(Bin_12), .Input_1(shift_add32_1_out_0), .Input_2(shift_add32_1_out_1),
    .Input_3(shift_add32_1_out_2), .out_0(shift_add32_2_out_0), .out_1(shift_add32_2_out_1),
    .out_2(shift_add32_2_out_2), .out_3(shift_add32_2_out_3));
  Shift_add32 shift_add32_3 (
    .Input_0(Bin_11), .Input_1(shift_add32_2_out_0), .Input_2(shift_add32_2_out_1),
    .Input_3(shift_add32_2_out_2), .out_0(shift_add32_3_out_0), .out_1(shift_add32_3_out_1),
    .out_2(shift_add32_3_out_2), .out_3(shift_add32_3_out_3));
  Shift_add32 shift_add32_4 (
    .Input_0(Bin_10), .Input_1(shift_add32_3_out_0), .Input_2(shift_add32_3_out_1),
    .Input_3(shift_add32_3_out_2), .out_0(shift_add32_4_out_0), .out_1(shift_add32_4_out_1),
    .out_2(shift_add32_4_out_2), .out_3(shift_add32_4_out_3));
  Shift_add32 shift_add32_5 (
    .Input_0(shift_add32_3_out_3), .Input_1(shift_add32_2_out_3), .Input_2(shift_add32_1_out_3),
    .Input_3(1'b0), .out_0(shift_add32_5_out_0), .out_1(shift_add32_5_out_1), .out_2(shift_add32_5_out_2),
    .out_3(shift_add32_5_out_3));
  Shift_add32 shift_add32_6 (
    .Input_0(shift_add32_4_out_3), .Input_1(shift_add32_5_out_0), .Input_2(shift_add32_5_out_1),
    .Input_3(shift_add32_5_out_2), .out_0(shift_add32_6_out_0), .out_1(shift_add32_6_out_1),
    .out_2(shift_add32_6_out_2), .out_3(shift_add32_6_out_3));
  Shift_add32 shift_add32_7 (
    .Input_0(Bin_9), .Input_1(shift_add32_4_out_0), .Input_2(shift_add32_4_out_1),
    .Input_3(shift_add32_4_out_2), .out_0(shift_add32_7_out_0), .out_1(shift_add32_7_out_1),
    .out_2(shift_add32_7_out_2), .out_3(shift_add32_7_out_3));
  Shift_add32 shift_add32_8 (
    .Input_0(Bin_8), .Input_1(shift_add32_7_out_0), .Input_2(shift_add32_7_out_1),
    .Input_3(shift_add32_7_out_2), .out_0(shift_add32_8_out_0), .out_1(shift_add32_8_out_1),
    .out_2(shift_add32_8_out_2), .out_3(shift_add32_8_out_3));
  Shift_add32 shift_add32_9 (
    .Input_0(shift_add32_7_out_3), .Input_1(shift_add32_6_out_0), .Input_2(shift_add32_6_out_1),
    .Input_3(shift_add32_6_out_2), .out_0(shift_add32_9_out_0), .out_1(shift_add32_9_out_1),
    .out_2(shift_add32_9_out_2), .out_3(shift_add32_9_out_3));
  Shift_add32 shift_add32_10 (
    .Input_0(Bin_7), .Input_1(shift_add32_8_out_0), .Input_2(shift_add32_8_out_1),
    .Input_3(shift_add32_8_out_2), .out_0(shift_add32_10_out_0), .out_1(shift_add32_10_out_1),
    .out_2(shift_add32_10_out_2), .out_3(shift_add32_10_out_3));
  Shift_add32 shift_add32_11 (
    .Input_0(shift_add32_8_out_3), .Input_1(shift_add32_9_out_0), .Input_2(shift_add32_9_out_1),
    .Input_3(shift_add32_9_out_2), .out_0(shift_add32_11_out_0), .out_1(shift_add32_11_out_1),
    .out_2(shift_add32_11_out_2), .out_3(shift_add32_11_out_3));
  Shift_add32 shift_add32_12 (
    .Input_0(shift_add32_9_out_3), .Input_1(shift_add32_6_out_3), .Input_2(shift_add32_5_out_3),
    .Input_3(1'b0), .out_0(shift_add32_12_out_0), .out_1(shift_add32_12_out_1), .out_2(shift_add32_12_out_2),
    .out_3(shift_add32_12_out_3));
  Shift_add32 shift_add32_13 (
    .Input_0(Bin_6), .Input_1(shift_add32_10_out_0), .Input_2(shift_add32_10_out_1),
    .Input_3(shift_add32_10_out_2), .out_0(shift_add32_13_out_0), .out_1(shift_add32_13_out_1),
    .out_2(shift_add32_13_out_2), .out_3(shift_add32_13_out_3));
  Shift_add32 shift_add32_14 (
    .Input_0(shift_add32_10_out_3), .Input_1(shift_add32_11_out_0), .Input_2(shift_add32_11_out_1),
    .Input_3(shift_add32_11_out_2), .out_0(shift_add32_14_out_0), .out_1(shift_add32_14_out_1),
    .out_2(shift_add32_14_out_2), .out_3(shift_add32_14_out_3));
  Shift_add32 shift_add32_15 (
    .Input_0(shift_add32_11_out_3), .Input_1(shift_add32_12_out_0), .Input_2(shift_add32_12_out_1),
    .Input_3(shift_add32_12_out_2), .out_0(shift_add32_15_out_0), .out_1(shift_add32_15_out_1),
    .out_2(shift_add32_15_out_2), .out_3(shift_add32_15_out_3));
  Shift_add32 shift_add32_16 (
    .Input_0(Bin_5), .Input_1(shift_add32_13_out_0), .Input_2(shift_add32_13_out_1),
    .Input_3(shift_add32_13_out_2), .out_0(shift_add32_16_out_0), .out_1(shift_add32_16_out_1),
    .out_2(shift_add32_16_out_2), .out_3(shift_add32_16_out_3));
  Shift_add32 shift_add32_17 (
    .Input_0(shift_add32_13_out_3), .Input_1(shift_add32_14_out_0), .Input_2(shift_add32_14_out_1),
    .Input_3(shift_add32_14_out_2), .out_0(shift_add32_17_out_0), .out_1(shift_add32_17_out_1),
    .out_2(shift_add32_17_out_2), .out_3(shift_add32_17_out_3));
  Shift_add32 shift_add32_18 (
    .Input_0(shift_add32_14_out_3), .Input_1(shift_add32_15_out_0), .Input_2(shift_add32_15_out_1),
    .Input_3(shift_add32_15_out_2), .out_0(shift_add32_18_out_0), .out_1(shift_add32_18_out_1),
    .out_2(shift_add32_18_out_2), .out_3(shift_add32_18_out_3));
  Shift_add32 shift_add32_19 (
    .Input_0(Bin_4), .Input_1(shift_add32_16_out_0), .Input_2(shift_add32_16_out_1),
    .Input_3(shift_add32_16_out_2), .out_0(shift_add32_19_out_0), .out_1(shift_add32_19_out_1),
    .out_2(shift_add32_19_out_2), .out_3(shift_add32_19_out_3));
  Shift_add32 shift_add32_20 (
    .Input_0(shift_add32_16_out_3), .Input_1(shift_add32_17_out_0), .Input_2(shift_add32_17_out_1),
    .Input_3(shift_add32_17_out_2), .out_0(shift_add32_20_out_0), .out_1(shift_add32_20_out_1),
    .out_2(shift_add32_20_out_2), .out_3(shift_add32_20_out_3));
  Shift_add32 shift_add32_21 (
    .Input_0(shift_add32_17_out_3), .Input_1(shift_add32_18_out_0), .Input_2(shift_add32_18_out_1),
    .Input_3(shift_add32_18_out_2), .out_0(shift_add32_21_out_0), .out_1(shift_add32_21_out_1),
    .out_2(shift_add32_21_out_2), .out_3(shift_add32_21_out_3));
  Shift_add32 shift_add32_22 (
    .Input_0(shift_add32_18_out_3), .Input_1(shift_add32_15_out_3), .Input_2(shift_add32_12_out_3),
    .Input_3(1'b0), .out_0(shift_add32_22_out_0), .out_1(shift_add32_22_out_1), .out_2(shift_add32_22_out_2),
    .out_3(shift_add32_22_out_3));
  Shift_add32 shift_add32_23 (
    .Input_0(Bin_3), .Input_1(shift_add32_19_out_0), .Input_2(shift_add32_19_out_1),
    .Input_3(shift_add32_19_out_2), .out_0(shift_add32_23_out_0), .out_1(shift_add32_23_out_1),
    .out_2(shift_add32_23_out_2), .out_3(shift_add32_23_out_3));
  Shift_add32 shift_add32_24 (
    .Input_0(shift_add32_19_out_3), .Input_1(shift_add32_20_out_0), .Input_2(shift_add32_20_out_1),
    .Input_3(shift_add32_20_out_2), .out_0(shift_add32_24_out_0), .out_1(shift_add32_24_out_1),
    .out_2(shift_add32_24_out_2), .out_3(shift_add32_24_out_3));
  Shift_add32 shift_add32_25 (
    .Input_0(shift_add32_20_out_3), .Input_1(shift_add32_21_out_0), .Input_2(shift_add32_21_out_1),
    .Input_3(shift_add32_21_out_2), .out_0(shift_add32_25_out_0), .out_1(shift_add32_25_out_1),
    .out_2(shift_add32_25_out_2), .out_3(shift_add32_25_out_3));
  Shift_add32 shift_add32_26 (
    .Input_0(shift_add32_21_out_3), .Input_1(shift_add32_22_out_0), .Input_2(shift_add32_22_out_1),
    .Input_3(shift_add32_22_out_2), .out_0(shift_add32_26_out_0), .out_1(shift_add32_26_out_1),
    .out_2(shift_add32_26_out_2), .out_3(shift_add32_26_out_3));
  Shift_add32 shift_add32_27 (
    .Input_0(Bin_2), .Input_1(shift_add32_23_out_0), .Input_2(shift_add32_23_out_1),
    .Input_3(shift_add32_23_out_2), .out_0(shift_add32_27_out_0), .out_1(shift_add32_27_out_1),
    .out_2(shift_add32_27_out_2), .out_3(shift_add32_27_out_3));
  Shift_add32 shift_add32_28 (
    .Input_0(shift_add32_23_out_3), .Input_1(shift_add32_24_out_0), .Input_2(shift_add32_24_out_1),
    .Input_3(shift_add32_24_out_2), .out_0(shift_add32_28_out_0), .out_1(shift_add32_28_out_1),
    .out_2(shift_add32_28_out_2), .out_3(shift_add32_28_out_3));
  Shift_add32 shift_add32_29 (
    .Input_0(shift_add32_24_out_3), .Input_1(shift_add32_25_out_0), .Input_2(shift_add32_25_out_1),
    .Input_3(shift_add32_25_out_2), .out_0(shift_add32_29_out_0), .out_1(shift_add32_29_out_1),
    .out_2(shift_add32_29_out_2), .out_3(shift_add32_29_out_3));
  Shift_add32 shift_add32_30 (
    .Input_0(shift_add32_25_out_3), .Input_1(shift_add32_26_out_0), .Input_2(shift_add32_26_out_1),
    .Input_3(shift_add32_26_out_2), .out_0(shift_add32_30_out_0), .out_1(shift_add32_30_out_1),
    .out_2(shift_add32_30_out_2), .out_3(shift_add32_30_out_3));
  Shift_add32 shift_add32_31 (
    .Input_0(Bin_1), .Input_1(shift_add32_27_out_0), .Input_2(shift_add32_27_out_1),
    .Input_3(shift_add32_27_out_2), .out_0(BCD_ones[1]), .out_1(BCD_ones[2]), .out_2(BCD_ones[3]),
    .out_3(BCD_Tens[0]));
  Shift_add32 shift_add32_32 (
    .Input_0(shift_add32_27_out_3), .Input_1(shift_add32_28_out_0), .Input_2(shift_add32_28_out_1),
    .Input_3(shift_add32_28_out_2), .out_0(BCD_Tens[1]), .out_1(BCD_Tens[2]), .out_2(BCD_Tens[3]),
    .out_3(BCD_Hundereds[0]));
  Shift_add32 shift_add32_33 (
    .Input_0(shift_add32_28_out_3), .Input_1(shift_add32_29_out_0), .Input_2(shift_add32_29_out_1),
    .Input_3(shift_add32_29_out_2), .out_0(BCD_Hundereds[1]), .out_1(BCD_Hundereds[2]),
    .out_2(BCD_Hundereds[3]), .out_3(BCD_Thousands[0]));
  Shift_add32 shift_add32_34 (
    .Input_0(shift_add32_29_out_3), .Input_1(shift_add32_30_out_0), .Input_2(shift_add32_30_out_1),
    .Input_3(shift_add32_30_out_2), .out_0(BCD_Thousands[1]), .out_1(BCD_Thousands[2]),
    .out_2(BCD_Thousands[3]), .out_3(BCD_Ten_Thousands[0]));
  Shift_add32 shift_add32_35 (
    .Input_0(shift_add32_30_out_3), .Input_1(shift_add32_26_out_3), .Input_2(shift_add32_22_out_3),
    .Input_3(1'b0), .out_0(BCD_Ten_Thousands[1]), .out_1(BCD_Ten_Thousands[2]), .out_2(BCD_Ten_Thousands[3]));  // open: out_3
  Hex_Digit_Display hex_digit_display_1 (.value({BCD_ones[3:1], Bin_0}));  // open: dp
  Hex_Digit_Display hex_digit_display_2 (.value(BCD_Tens));  // open: dp
  Hex_Digit_Display hex_digit_display_3 (.value(BCD_Hundereds));  // open: dp
  Hex_Digit_Display hex_digit_display_4 (.value(BCD_Thousands));  // open: dp
  Hex_Digit_Display hex_digit_display_5 (.value(BCD_Ten_Thousands));  // open: dp

  assign BCD_ones[0] = Bin_0;
endmodule

module Control_unit (
  input  reset,
  input  BTNC,
  input  b0,
  input  Clk,
  input  BTNL,
  input  BTNR,
  input  Enable,
  input  Z_flag,
  output rst,
  output LA,
  output LB,
  output Psel,
  output [1:0] Sel,
  output EB,
  output EP,
  output EA,
  output Done
);

  wire and_2_out, BTNLB, d_ff_1_q, multiplexer_1_out, multiplexer_2_out, not_1_out;

  not not_1 (not_1_out, Z_flag);
  and and_1 (EA, Enable, not_1_out);
  not not_2 (BTNLB, BTNL);
  Multiplexer multiplexer_1 (.in0(BTNLB), .in1(BTNR), .out(multiplexer_1_out), .sel(BTNR));
  and and_2 (and_2_out, BTNL, BTNR);
  Multiplexer multiplexer_2 (.in0(multiplexer_1_out), .in1(d_ff_1_q), .out(multiplexer_2_out), .sel(BTNLB));
  D_Flip_Flop d_ff_1 (.clk(Clk), .D(multiplexer_2_out), .Q(d_ff_1_q), .reset(reset));  // open: Qn, preset
  Counter #(.max('h3), .width(2)) counter_1 (
    .D(Sel), .count(Z_flag), .Q(Sel), .up(d_ff_1_q), .clk(Clk), .clr(reset));  // open: load, carry

  assign Done = Z_flag;
  assign EB = EA;
  assign EP = EA;
  assign LA = BTNC;
  assign LB = BTNC;
  assign Psel = b0;
  assign rst = reset;

  // Other names for the same wires on the sheet: A = BTNL; B = BTNR; Clkout = Clk
endmodule
