// Logisim project DD1_project2_new.circ as structural Verilog: 2 circuits, main circuit main
module main (
  input  Bin_0,
  input  Bin_1,
  input  Bin_2,
  input  Bin_3,
  input  Bin_4,
  input  Bin_5,
  input  Bin_6,
  input  Bin_7,
  input  Bin_8,
  input  Bin_9,
  input  Bin_10,
  input  Bin_11,
  input  Bin_12,
  input  Bin_13,
  input  Bin_14,
  input  Bin_15,
  output [3:0] BCD_ones,
  output [3:0] BCD_Tens,
  output [3:0] BCD_Hundereds,
  output [3:0] BCD_Thousands,
  output [3:0] BCD_Ten_Thousands
);

  wire shift_add32_1_out_0, shift_add32_1_out_1, shift_add32_1_out_2, shift_add32_1_out_3,
       shift_add32_2_out_0, shift_add32_2_out_1, shift_add32_2_out_2, shift_add32_2_out_3,
       shift_add32_3_out_0, shift_add32_3_out_1, shift_add32_3_out_2, shift_add32_3_out_3,
       shift_add32_4_out_0, shift_add32_4_out_1, shift_add32_4_out_2, shift_add32_4_out_3,
       shift_add32_5_out_0, shift_add32_5_out_1, shift_add32_5_out_2, shift_add32_5_out_3,
       shift_add32_6_out_0, shift_add32_6_out_1, shift_add32_6_out_2, shift_add32_6_out_3,
       shift_add32_7_out_0, shift_add32_7_out_1, shift_add32_7_out_2, shift_add32_7_out_3,
       shift_add32_8_out_0, shift_add32_8_out_1, shift_add32_8_out_2, shift_add32_8_out_3,
       shift_add32_9_out_0, shift_add32_9_out_1, shift_add32_9_out_2, shift_add32_9_out_3,
       shift_add32_10_out_0, shift_add32_10_out_1, shift_add32_10_out_2, shift_add32_10_out_3,
       shift_add32_11_out_0, shift_add32_11_out_1, shift_add32_11_out_2, shift_add32_11_out_3,
       shift_add32_12_out_0, shift_add32_12_out_1, shift_add32_12_out_2, shift_add32_12_out_3,
       shift_add32_13_out_0, shift_add32_13_out_1, shift_add32_13_out_2, shift_add32_13_out_3,
       shift_add32_14_out_0, shift_add32_14_out_1, shift_add32_14_out_2, shift_add32_14_out_3,
       shift_add32_15_out_0, shift_add32_15_out_1, shift_add32_15_out_2, shift_add32_15_out_3,
       shift_add32_16_out_0, shift_add32_16_out_1, shift_add32_16_out_2, shift_add32_16_out_3,
       shift_add32_17_out_0, shift_add32_17_out_1, shift_add32_17_out_2, shift_add32_17_out_3,
       shift_add32_18_out_0, shift_add32_18_out_1, shift_add32_18_out_2, shift_add32_18_out_3,
       shift_add32_19_out_0, shift_add32_19_out_1, shift_add32_19_out_2, shift_add32_19_out_3,
       shift_add32_20_out_0, shift_add32_20_out_1, shift_add32_20_out_2, shift_add32_20_out_3,
       shift_add32_21_out_0, shift_add32_21_out_1, shift_add32_21_out_2, shift_add32_21_out_3,
       shift_add32_22_out_0, shift_add32_22_out_1, shift_add32_22_out_2, shift_add32_22_out_3,
       shift_add32_23_out_0, shift_add32_23_out_1, shift_add32_23_out_2, shift_add32_23_out_3,
       shift_add32_24_out_0, shift_add32_24_out_1, shift_add32_24_out_2, shift_add32_24_out_3,
       shift_add32_25_out_0, shift_add32_25_out_1, shift_add32_25_out_2, shift_add32_25_out_3,
       shift_add32_26_out_0, shift_add32_26_out_1, shift_add32_26_out_2, shift_add32_26_out_3,
       shift_add32_27_out_0, shift_add32_27_out_1, shift_add32_27_out_2, shift_add32_27_out_3,
       shift_add32_28_out_0, shift_add32_28_out_1, shift_add32_28_out_2, shift_add32_28_out_3,
       shift_add32_29_out_0, shift_add32_29_out_1, shift_add32_29_out_2, shift_add32_29_out_3,
       shift_add32_30_out_0, shift_add32_30_out_1, shift_add32_30_out_2, shift_add32_30_out_3;

  shift_add32 shift_add32_1 (
    .Input_0(Bin_13), .Input_1(Bin_14), .Input_2(Bin_15), .Input_3(1'b0), .out_0(shift_add32_1_out_0),
    .out_1(shift_add32_1_out_1), .out_2(shift_add32_1_out_2), .out_3(shift_add32_1_out_3));
  shift_add32 shift_add32_2 (
    .Input_0(Bin_12), .Input_1(shift_add32_1_out_0), .Input_2(shift_add32_1_out_1),
    .Input_3(shift_add32_1_out_2), .out_0(shift_add32_2_out_0), .out_1(shift_add32_2_out_1),
    .out_2(shift_add32_2_out_2), .out_3(shift_add32_2_out_3));
  shift_add32 shift_add32_3 (
    .Input_0(Bin_11), .Input_1(shift_add32_2_out_0), .Input_2(shift_add32_2_out_1),
    .Input_3(shift_add32_2_out_2), .out_0(shift_add32_3_out_0), .out_1(shift_add32_3_out_1),
    .out_2(shift_add32_3_out_2), .out_3(shift_add32_3_out_3));
  shift_add32 shift_add32_4 (
    .Input_0(Bin_10), .Input_1(shift_add32_3_out_0), .Input_2(shift_add32_3_out_1),
    .Input_3(shift_add32_3_out_2), .out_0(shift_add32_4_out_0), .out_1(shift_add32_4_out_1),
    .out_2(shift_add32_4_out_2), .out_3(shift_add32_4_out_3));
  shift_add32 shift_add32_5 (
    .Input_0(shift_add32_3_out_3), .Input_1(shift_add32_2_out_3), .Input_2(shift_add32_1_out_3),
    .Input_3(1'b0), .out_0(shift_add32_5_out_0), .out_1(shift_add32_5_out_1), .out_2(shift_add32_5_out_2),
    .out_3(shift_add32_5_out_3));
  shift_add32 shift_add32_6 (
    .Input_0(shift_add32_4_out_3), .Input_1(shift_add32_5_out_0), .Input_2(shift_add32_5_out_1),
    .Input_3(shift_add32_5_out_2), .out_0(shift_add32_6_out_0), .out_1(shift_add32_6_out_1),
    .out_2(shift_add32_6_out_2), .out_3(shift_add32_6_out_3));
  shift_add32 shift_add32_7 (
    .Input_0(Bin_9), .Input_1(shift_add32_4_out_0), .Input_2(shift_add32_4_out_1),
    .Input_3(shift_add32_4_out_2), .out_0(shift_add32_7_out_0), .out_1(shift_add32_7_out_1),
    .out_2(shift_add32_7_out_2), .out_3(shift_add32_7_out_3));
  shift_add32 shift_add32_8 (
    .Input_0(Bin_8), .Input_1(shift_add32_7_out_0), .Input_2(shift_add32_7_out_1),
    .Input_3(shift_add32_7_out_2), .out_0(shift_add32_8_out_0), .out_1(shift_add32_8_out_1),
    .out_2(shift_add32_8_out_2), .out_3(shift_add32_8_out_3));
  shift_add32 shift_add32_9 (
    .Input_0(shift_add32_7_out_3), .Input_1(shift_add32_6_out_0), .Input_2(shift_add32_6_out_1),
    .Input_3(shift_add32_6_out_2), .out_0(shift_add32_9_out_0), .out_1(shift_add32_9_out_1),
    .out_2(shift_add32_9_out_2), .out_3(shift_add32_9_out_3));
  shift_add32 shift_add32_10 (
    .Input_0(Bin_7), .Input_1(shift_add32_8_out_0), .Input_2(shift_add32_8_out_1),
    .Input_3(shift_add32_8_out_2), .out_0(shift_add32_10_out_0), .out_1(shift_add32_10_out_1),
    .out_2(shift_add32_10_out_2), .out_3(shift_add32_10_out_3));
  shift_add32 shift_add32_11 (
    .Input_0(shift_add32_8_out_3), .Input_1(shift_add32_9_out_0), .Input_2(shift_add32_9_out_1),
    .Input_3(shift_add32_9_out_2), .out_0(shift_add32_11_out_0), .out_1(shift_add32_11_out_1),
    .out_2(shift_add32_11_out_2), .out_3(shift_add32_11_out_3));
  shift_add32 shift_add32_12 (
    .Input_0(shift_add32_9_out_3), .Input_1(shift_add32_6_out_3), .Input_2(shift_add32_5_out_3),
    .Input_3(1'b0), .out_0(shift_add32_12_out_0), .out_1(shift_add32_12_out_1), .out_2(shift_add32_12_out_2),
    .out_3(shift_add32_12_out_3));
  shift_add32 shift_add32_13 (
    .Input_0(Bin_6), .Input_1(shift_add32_10_out_0), .Input_2(shift_add32_10_out_1),
    .Input_3(shift_add32_10_out_2), .out_0(shift_add32_13_out_0), .out_1(shift_add32_13_out_1),
    .out_2(shift_add32_13_out_2), .out_3(shift_add32_13_out_3));
  shift_add32 shift_add32_14 (
    .Input_0(shift_add32_10_out_3), .Input_1(shift_add32_11_out_0), .Input_2(shift_add32_11_out_1),
    .Input_3(shift_add32_11_out_2), .out_0(shift_add32_14_out_0), .out_1(shift_add32_14_out_1),
    .out_2(shift_add32_14_out_2), .out_3(shift_add32_14_out_3));
  shift_add32 shift_add32_15 (
    .Input_0(shift_add32_11_out_3), .Input_1(shift_add32_12_out_0), .Input_2(shift_add32_12_out_1),
    .Input_3(shift_add32_12_out_2), .out_0(shift_add32_15_out_0), .out_1(shift_add32_15_out_1),
    .out_2(shift_add32_15_out_2), .out_3(shift_add32_15_out_3));
  shift_add32 shift_add32_16 (
    .Input_0(Bin_5), .Input_1(shift_add32_13_out_0), .Input_2(shift_add32_13_out_1),
    .Input_3(shift_add32_13_out_2), .out_0(shift_add32_16_out_0), .out_1(shift_add32_16_out_1),
    .out_2(shift_add32_16_out_2), .out_3(shift_add32_16_out_3));
  shift_add32 shift_add32_17 (
    .Input_0(shift_add32_13_out_3), .Input_1(shift_add32_14_out_0), .Input_2(shift_add32_14_out_1),
    .Input_3(shift_add32_14_out_2), .out_0(shift_add32_17_out_0), .out_1(shift_add32_17_out_1),
    .out_2(shift_add32_17_out_2), .out_3(shift_add32_17_out_3));
  shift_add32 shift_add32_18 (
    .Input_0(shift_add32_14_out_3), .Input_1(shift_add32_15_out_0), .Input_2(shift_add32_15_out_1),
    .Input_3(shift_add32_15_out_2), .out_0(shift_add32_18_out_0), .out_1(shift_add32_18_out_1),
    .out_2(shift_add32_18_out_2), .out_3(shift_add32_18_out_3));
  shift_add32 shift_add32_19 (
    .Input_0(Bin_4), .Input_1(shift_add32_16_out_0), .Input_2(shift_add32_16_out_1),
    .Input_3(shift_add32_16_out_2), .out_0(shift_add32_19_out_0), .out_1(shift_add32_19_out_1),
    .out_2(shift_add32_19_out_2), .out_3(shift_add32_19_out_3));
  shift_add32 shift_add32_20 (
    .Input_0(shift_add32_16_out_3), .Input_1(shift_add32_17_out_0), .Input_2(shift_add32_17_out_1),
    .Input_3(shift_add32_17_out_2), .out_0(shift_add32_20_out_0), .out_1(shift_add32_20_out_1),
    .out_2(shift_add32_20_out_2), .out_3(shift_add32_20_out_3));
  shift_add32 shift_add32_21 (
    .Input_0(shift_add32_17_out_3), .Input_1(shift_add32_18_out_0), .Input_2(shift_add32_18_out_1),
    .Input_3(shift_add32_18_out_2), .out_0(shift_add32_21_out_0), .out_1(shift_add32_21_out_1),
    .out_2(shift_add32_21_out_2), .out_3(shift_add32_21_out_3));
  shift_add32 shift_add32_22 (
    .Input_0(shift_add32_18_out_3), .Input_1(shift_add32_15_out_3), .Input_2(shift_add32_12_out_3),
    .Input_3(1'b0), .out_0(shift_add32_22_out_0), .out_1(shift_add32_22_out_1), .out_2(shift_add32_22_out_2),
    .out_3(shift_add32_22_out_3));
  shift_add32 shift_add32_23 (
    .Input_0(Bin_3), .Input_1(shift_add32_19_out_0), .Input_2(shift_add32_19_out_1),
    .Input_3(shift_add32_19_out_2), .out_0(shift_add32_23_out_0), .out_1(shift_add32_23_out_1),
    .out_2(shift_add32_23_out_2), .out_3(shift_add32_23_out_3));
  shift_add32 shift_add32_24 (
    .Input_0(shift_add32_19_out_3), .Input_1(shift_add32_20_out_0), .Input_2(shift_add32_20_out_1),
    .Input_3(shift_add32_20_out_2), .out_0(shift_add32_24_out_0), .out_1(shift_add32_24_out_1),
    .out_2(shift_add32_24_out_2), .out_3(shift_add32_24_out_3));
  shift_add32 shift_add32_25 (
    .Input_0(shift_add32_20_out_3), .Input_1(shift_add32_21_out_0), .Input_2(shift_add32_21_out_1),
    .Input_3(shift_add32_21_out_2), .out_0(shift_add32_25_out_0), .out_1(shift_add32_25_out_1),
    .out_2(shift_add32_25_out_2), .out_3(shift_add32_25_out_3));
  shift_add32 shift_add32_26 (
    .Input_0(shift_add32_21_out_3), .Input_1(shift_add32_22_out_0), .Input_2(shift_add32_22_out_1),
    .Input_3(shift_add32_22_out_2), .out_0(shift_add32_26_out_0), .out_1(shift_add32_26_out_1),
    .out_2(shift_add32_26_out_2), .out_3(shift_add32_26_out_3));
  shift_add32 shift_add32_27 (
    .Input_0(Bin_2), .Input_1(shift_add32_23_out_0), .Input_2(shift_add32_23_out_1),
    .Input_3(shift_add32_23_out_2), .out_0(shift_add32_27_out_0), .out_1(shift_add32_27_out_1),
    .out_2(shift_add32_27_out_2), .out_3(shift_add32_27_out_3));
  shift_add32 shift_add32_28 (
    .Input_0(shift_add32_23_out_3), .Input_1(shift_add32_24_out_0), .Input_2(shift_add32_24_out_1),
    .Input_3(shift_add32_24_out_2), .out_0(shift_add32_28_out_0), .out_1(shift_add32_28_out_1),
    .out_2(shift_add32_28_out_2), .out_3(shift_add32_28_out_3));
  shift_add32 shift_add32_29 (
    .Input_0(shift_add32_24_out_3), .Input_1(shift_add32_25_out_0), .Input_2(shift_add32_25_out_1),
    .Input_3(shift_add32_25_out_2), .out_0(shift_add32_29_out_0), .out_1(shift_add32_29_out_1),
    .out_2(shift_add32_29_out_2), .out_3(shift_add32_29_out_3));
  shift_add32 shift_add32_30 (
    .Input_0(shift_add32_25_out_3), .Input_1(shift_add32_26_out_0), .Input_2(shift_add32_26_out_1),
    .Input_3(shift_add32_26_out_2), .out_0(shift_add32_30_out_0), .out_1(shift_add32_30_out_1),
    .out_2(shift_add32_30_out_2), .out_3(shift_add32_30_out_3));
  shift_add32 shift_add32_31 (
    .Input_0(Bin_1), .Input_1(shift_add32_27_out_0), .Input_2(shift_add32_27_out_1),
    .Input_3(shift_add32_27_out_2), .out_0(BCD_ones[1]), .out_1(BCD_ones[2]), .out_2(BCD_ones[3]),
    .out_3(BCD_Tens[0]));
  shift_add32 shift_add32_32 (
    .Input_0(shift_add32_27_out_3), .Input_1(shift_add32_28_out_0), .Input_2(shift_add32_28_out_1),
    .Input_3(shift_add32_28_out_2), .out_0(BCD_Tens[1]), .out_1(BCD_Tens[2]), .out_2(BCD_Tens[3]),
    .out_3(BCD_Hundereds[0]));
  shift_add32 shift_add32_33 (
    .Input_0(shift_add32_28_out_3), .Input_1(shift_add32_29_out_0), .Input_2(shift_add32_29_out_1),
    .Input_3(shift_add32_29_out_2), .out_0(BCD_Hundereds[1]), .out_1(BCD_Hundereds[2]),
    .out_2(BCD_Hundereds[3]), .out_3(BCD_Thousands[0]));
  shift_add32 shift_add32_34 (
    .Input_0(shift_add32_29_out_3), .Input_1(shift_add32_30_out_0), .Input_2(shift_add32_30_out_1),
    .Input_3(shift_add32_30_out_2), .out_0(BCD_Thousands[1]), .out_1(BCD_Thousands[2]),
    .out_2(BCD_Thousands[3]), .out_3(BCD_Ten_Thousands[0]));
  shift_add32 shift_add32_35 (
    .Input_0(shift_add32_30_out_3), .Input_1(shift_add32_26_out_3), .Input_2(shift_add32_22_out_3),
    .Input_3(1'b0), .out_0(BCD_Ten_Thousands[1]), .out_1(BCD_Ten_Thousands[2]), .out_2(BCD_Ten_Thousands[3]));  // open: out_3
  Hex_Digit_Display hex_digit_display_1 (.value({BCD_ones[3:1], Bin_0}));  // open: dp
  Hex_Digit_Display hex_digit_display_2 (.value(BCD_Tens));  // open: dp
  Hex_Digit_Display hex_digit_display_3 (.value(BCD_Hundereds));  // open: dp
  Hex_Digit_Display hex_digit_display_4 (.value(BCD_Thousands));  // open: dp
  Hex_Digit_Display hex_digit_display_5 (.value(BCD_Ten_Thousands));  // open: dp

  assign BCD_ones[0] = Bin_0;
endmodule

module shift_add32 (
  input  Input_0,
  input  Input_1,
  input  Input_2,
  input  Input_3,
  output out_0,
  output out_1,
  output out_2,
  output out_3
);

  wire comparator_1_gt;
  wire [3:0] adder_1_out;

  Adder #(.width(4)) adder_1 (
    .a(4'b0011), .b({Input_3, Input_2, Input_1, Input_0}), .out(adder_1_out), .cin(1'b0));  // open: cout
  Comparator #(.mode("unsigned"), .width(4)) comparator_1 (
    .a({Input_3, Input_2, Input_1, Input_0}), .b(4'b0100), .gt(comparator_1_gt));  // open: eq, lt
  Multiplexer #(.width(4)) multiplexer_1 (
    .in0({Input_3, Input_2, Input_1, Input_0}), .in1(adder_1_out), .out({out_3, out_2, out_1, out_0}),
    .sel(comparator_1_gt));
endmodule
